# Fritzing sketch Remote.01 (saved by Fritzing 0.9.2b)
breadboards: 1

parts:
  Anarduino_actually = Arduino Nano (Rev3.0)
  LCD1_20x4 = LCD screen
  R1_10K = TRIMPOT [package=3362u-2]
  Radio = RFM69 [package=rfm69-xxx-s2]
  P1 = NCP1400 Step-Up Breakout
  4xAA_NiMh = 4 x AAA Battery Mount

nets:
  GND: Anarduino_actually.GND, Anarduino_actually.D2, LCD1_20x4.VSS, LCD1_20x4.R/W, LCD1_20x4.LED-, R1_10K.CW, Radio.DIO0, Radio.GND, Radio.NC, P1.GND, 4xAA_NiMh.-
  N1: Anarduino_actually.D4, LCD1_20x4.DB4
  N2: Anarduino_actually.D5, LCD1_20x4.DB5
  N3: Anarduino_actually.D6, LCD1_20x4.DB6
  N4: Anarduino_actually.D7, LCD1_20x4.DB7
  N5: Anarduino_actually.D8, LCD1_20x4.RS
  N6: Anarduino_actually.D9, LCD1_20x4.E
  N7: Anarduino_actually.D10, Radio.NSS
  N8: Anarduino_actually.D11/MOSI, Radio.MOSI
  N9: Anarduino_actually.D12/MISO, Radio.MISO
  5V: Anarduino_actually.VIN, LCD1_20x4.VDD, LCD1_20x4.LED+, R1_10K.CCW, P1.VOUT
  3.3V: Anarduino_actually.3V3, Radio.VCC
  N10: Anarduino_actually.D13/SCK, Radio.SCK
  N11: LCD1_20x4.V0, R1_10K.WIPER
  N12: P1.VIN, 4xAA_NiMh.+

notes:
  Video Slide/Pan/Tilt Controller, Remote for  Slide/Pan/Tilt Controller, 0.1

custom parts:
  RFM69: The RFM69 is a low-power, low cost radio that is capable of operating in the 434MHz and 900MHz open bands. It's frequency is software defined and there are some very good libraries written for it.
