# Fritzing sketch SlidePanTilt.01 (saved by Fritzing 0.9.2b)
breadboards: 1

parts:
  Part1 = Arduino Mega 2560 (Rev3)
  Part2 = Motor Driver 1A Dual TB6612FNG
  Pan_Motor = DC Motor
  Tilt_Motor = DC Motor
  Slide_Motor = DC Motor
  Part4 = DeuLigne 1.1 - The Snootlab's LCD shield for Arduino
  Part3 = Motor Driver 1A Dual TB6612FNG
  Left_EndSwitch = Pushbutton [package=THT]
  Right_EndSwitch1 = Pushbutton [package=THT]
  U1A = RJ45 Jack [package=rj45-8]
  U2A = RJ45 Jack [package=rj45-8]
  U2B = RJ45 Jack [package=rj45-8]
  U!B = RJ45 Jack [package=rj45-8]

nets:
  N1: Part1.A0, Part4.A0
  GND: Part1.GND, Part2.GND, Part4.GND, Part3.GND, U2A.1
  N2: Part1.D12_PWM, Part2.PWMB
  N3: Part1.D11_PWM, Part2.PWMA
  N4: Part1.D10_PWM, Part4.D10_SS
  N5: Part1.D9_PWM, Part4.D9
  N6: Part1.D8_PWM, Part4.D8
  N7: Part1.IOREF, Part4.+5V
  VCC: Part1.3V3, Part2.VCC, Part2.STBY, Part3.VCC, Part3.STBY
  VIN: Part1.VIN, Part4.VIN
  N8: Part1.D2_PWM, U2A.2
  N9: Part1.D3_PWM, Part3.PWMA
  N10: Part1.D4_PWM, Part4.D4
  N11: Part1.D5_PWM, Part4.D5
  N12: Part1.D6_PWM, Part4.D6
  N13: Part1.D7_PWM, Part4.D7
  N14: Part1.D22, Part2.AIN1
  N15: Part1.D23, Part2.AIN2
  N16: Part1.D24, Part2.BIN1
  N17: Part1.D25, Part2.BIN2
  N18: Part1.D26, Part3.AIN1
  N19: Part1.D27, Part3.AIN2
  N20: Part2.B01, U1A.3
  N21: Part2.B02, U1A.6
  N22: Part2.A02, U1A.5
  N23: Part2.A01, U1A.4
  N24: Pan_Motor.pin_1, U!B.4
  N25: Pan_Motor.pin_2, U!B.5
  N26: Tilt_Motor.pin_1, U!B.3
  N27: Tilt_Motor.pin_2, U!B.6
  N28: Slide_Motor.pin_1, U2B.4
  N29: Slide_Motor.pin_2, U2B.5
  N30: Part3.A02, U2A.5
  N31: Part3.A01, U2A.4
  N32: Left_EndSwitch.leg0, Right_EndSwitch1.leg0, U2B.2
  N33: Left_EndSwitch.leg1, Right_EndSwitch1.leg1, U2B.1
