# Fritzing sketch SlidePanTilt.02 (saved by Fritzing 0.9.2b)
perfboards: 2

parts:
  Part6 = Arduino Mega 2560 (Rev3)
  Pan/Tilt_Motor_Driver = Motor Driver 1A Dual TB6612FNG
  Pan_Motor_RF500T = DC Motor
  Tilt_Motor_RF500T = DC Motor
  Slide_Motor_25GA-226-10_5D = DC Motor
  Part4 = DeuLigne 1.1 - The Snootlab's LCD shield for Arduino
  Slide_Motor_Driver = Motor Driver 1A Dual TB6612FNG
  Left_EndSwitch = Pushbutton [package=THT]
  Right_EndSwitch = Pushbutton [package=THT]
  U1A = RJ45 Jack [package=rj45-8]
  U2A = RJ45 Jack [package=rj45-8]
  U2B = RJ45 Jack [package=rj45-8]
  U1B = RJ45 Jack [package=rj45-8]
  Power_plug_12V_2_5mm = Power plug
  U3 = LM3480IM4 [package=sot23-3]
  R2 = Resistor [tolerance=±5% resistance=15k package=THT]
  R1 = Resistor [tolerance=±5% resistance=100k package=THT]
  C1 = Ceramic Capacitor [capacitance=1µF package="100 mil [THT, multilayer]"]
  90_EndSwitch = Pushbutton [package=THT]
  45_EndSwitch = Pushbutton [package=THT]
  340_EndSwitch = Pushbutton [package=THT]
  JP2 = Header for Motor with Encoder [package=molex-1x6-ra]

nets:
  N1: Part6.A0, Part4.A0
  GND: Part6.GND, Slide_Motor_Driver.GND, U1A.1, U2A.1, Power_plug_12V_2_5mm.GND, U3.GND, C1.0
  N2: Part6.D12_PWM, Pan/Tilt_Motor_Driver.PWMB
  N3: Part6.D11_PWM, Pan/Tilt_Motor_Driver.PWMA
  N4: Part6.D10_PWM, Part4.D10_SS
  N5: Part6.D9_PWM, Part4.D9
  N6: Part6.D8_PWM, Part4.D8
  N7: Part6.IOREF, Part4.+5V
  3.3V: Part6.3V3, Pan/Tilt_Motor_Driver.VCC, Pan/Tilt_Motor_Driver.STBY, Part4.+3V3, Slide_Motor_Driver.VCC, Slide_Motor_Driver.STBY
  7V: Part6.VIN, Pan/Tilt_Motor_Driver.VM, Part4.VIN, U3.OUT
  N8: Part6.D2_PWM, R2.Pin_0, C1.1
  N9: Part6.D3_PWM, Slide_Motor_Driver.PWMA
  N10: Part6.D4_PWM, Part4.D4
  N11: Part6.D5_PWM, Part4.D5
  N12: Part6.D6_PWM, Part4.D6
  N13: Part6.D7_PWM, Part4.D7
  N14: Part6.D22, Pan/Tilt_Motor_Driver.AIN1
  N15: Part6.D23, Pan/Tilt_Motor_Driver.AIN2
  N16: Part6.D24, Pan/Tilt_Motor_Driver.BIN1
  N17: Part6.D25, Pan/Tilt_Motor_Driver.BIN2
  N18: Part6.D26, Slide_Motor_Driver.AIN1
  N19: Part6.D27, Slide_Motor_Driver.AIN2
  N20: Pan/Tilt_Motor_Driver.B01, U1A.3
  N21: Pan/Tilt_Motor_Driver.B02, U1A.6
  N22: Pan/Tilt_Motor_Driver.A02, U1A.5
  N23: Pan/Tilt_Motor_Driver.A01, U1A.4
  N24: Pan_Motor_RF500T.pin_1, U1B.4
  N25: Pan_Motor_RF500T.pin_2, U1B.5
  N26: Tilt_Motor_RF500T.pin_1, U1B.3
  N27: Tilt_Motor_RF500T.pin_2, U1B.6
  N28: Slide_Motor_25GA-226-10_5D.pin_1, U2B.3, U2B.4, JP2.M1
  N29: Slide_Motor_25GA-226-10_5D.pin_2, U2B.5, U2B.6, JP2.M2
  N30: Slide_Motor_Driver.A02, U2A.5, U2A.6
  N31: Slide_Motor_Driver.A01, U2A.3, U2A.4
  12V: Slide_Motor_Driver.VM, Power_plug_12V_2_5mm.VCC, U3.IN
  N32: Left_EndSwitch.leg0, Right_EndSwitch.leg0, U2B.2
  N33: Left_EndSwitch.leg1, Right_EndSwitch.leg1, U2B.1, JP2.Gnd
  N34: U2A.2, R2.Pin_1, R1.Pin_1
  N35: U2B.7, JP2.EncA
  N36: U2B.8, JP2.EncB
  N37: U1B.1, 90_EndSwitch.leg1, 45_EndSwitch.leg1, 340_EndSwitch.leg1
  N38: U1B.2, 45_EndSwitch.leg0
  N39: U1B.7, 90_EndSwitch.leg0
  N40: U1B.8, 340_EndSwitch.leg0

notes:
  Video Slide/Pan/Tilt Controller, Video Slide/Pan/Tilt Controller Schematcis, 1.0

custom parts:
  Header for Motor with Encoder: Header 6 Standard 6-pin 0.1 header. Use with straight break away headers (SKU : PRT-00116), right angle break away headers (PRT-00553), swiss pins (PRT-00743), machine pins (PRT-00117), and female headers (PRT-00115). Molex polarized connector foot print use with SKU : PRT-08094 with associated crimp pins and housings. NOTES ON THE VARIANTS LOCK and LOCK_LONGPADS... This footprint was designed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
